# Fritzing sketch ac_circuits (saved by Fritzing 0.9.3b)
breadboards: 2

parts:
  Part1 = Adafruit Metro Mini [part_number="Adafruit #2590"]
  Part2 = Adafruit Metro Mini [part_number="Adafruit #2590"]
  IR1 = TSOP312.., 314.. [package=THT]
  D1 = LTE-302 [package=lte-302]
  U1 = TRANSISTOR_NPN_2 [package=to-92]
  R1 = Resistor [tolerance=±5% resistance=470 package="2010 [SMD]"]

nets:
  N1: Part1.IO11, IR1.Data
  N2: Part1.+5V, IR1.Vs
  GND: Part1.GND, IR1.GND
  N3: Part2.IO2, R1.Pin_0
  N4: Part2.+5V, D1.A
  N5: Part2.GND, U1.E
  N6: D1.C, U1.C
  N7: U1.B, R1.Pin_1

custom parts:
  Adafruit Metro Mini: We sure love the ATmega328 here at Adafruit, and we use them a lot for our own projects. The processor has plenty of GPIO, Analog inputs, hardware UART SPI and I2C, timers and PWM galore - just enough for most simple projects. When we need to go small, we use a Pro Trinket 3V or 5V, but if you want to have USB-to-Serial built in, we reach for an Adafruit METRO Mini. METRO Mini is the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
